// Logisim project D8421.circ as structural Verilog: 1 circuit, main circuit main
module main (
  input  [3:0] in_1,
  input  [3:0] in_2,
  output [3:0] out_3,
  output [3:0] out_4,
  output [3:0] out_5,
  output [3:0] out_6
);

  wire and_1_out, and_2_out, and_3_out, and_4_out, and_5_out, and_6_out, and_7_out, or_1_out, or_2_out;

  xor xor_1 (out_4[0], in_1[0], in_2[0]);
  and and_1 (and_1_out, in_2[0], in_1[0]);
  and and_2 (and_2_out, in_1[1], in_2[1]);
  and and_3 (and_3_out, in_1[1], and_1_out);
  and and_4 (and_4_out, and_1_out, in_2[1]);
  ExactlyOne xor_2 (.out(out_4[1]), .in0(and_1_out), .in1(in_1[1]), .in2(in_2[1]));
  or or_1 (or_1_out, and_2_out, and_3_out, and_4_out);
  ExactlyOne xor_3 (.out(out_4[2]), .in0(in_1[2]), .in1(or_1_out), .in2(in_2[2]));
  and and_5 (and_5_out, or_1_out, in_1[2]);
  and and_6 (and_6_out, or_1_out, in_2[2]);
  and and_7 (and_7_out, in_1[2], in_2[2]);
  or or_2 (or_2_out, and_5_out, and_6_out, and_7_out);
  ExactlyOne xor_4 (.out(out_4[3]), .in0(in_1[3]), .in1(or_2_out), .in2(in_2[3]));

  assign out_3 = in_1;
  assign out_5 = out_4;
  assign out_6 = in_2;
endmodule
