// Logisim project VendingMachine.circ as structural Verilog: 1 circuit, main circuit main
module main (
  output [2:0] out_1,
  output [2:0] out_2
);

  wire and_1_out, clock_1_out;

  and and_1 (and_1_out, out_1[1], out_1[0]);
  Clock clock_1 (.out(clock_1_out));
  T_Flip_Flop t_ff_1 (.T(and_1_out), .clk(clock_1_out), .Q(out_1[2]));  // open: Qn, reset, preset
  T_Flip_Flop t_ff_2 (.T(out_1[0]), .clk(clock_1_out), .Q(out_1[1]));  // open: Qn, reset, preset
  T_Flip_Flop t_ff_3 (.T(1'b1), .clk(clock_1_out), .Q(out_1[0]));  // open: Qn, reset, preset

  assign out_2 = out_1;

  // Other names for the same wires on the sheet: Q2 = out_1[0]; Q1 = out_1[1]; Q0 = out_1[2]
endmodule
